// Logisim project Parity_Checker_Project.circ as structural Verilog: 1 circuit, main circuit main
module main (
  input  in_1,
  input  in_2,
  input  in_3,
  input  in_4,
  input  in_5,
  input  in_6,
  input  in_7,
  input  in_8,
  input  in_9,
  output out_10,
  output out_11
);

  wire xor_1_out, xor_2_out, xor_3_out, xor_4_out, xor_6_out;

  xor xor_1 (xor_1_out, in_1, in_2);
  xor xor_2 (xor_2_out, in_3, in_4);
  xor xor_3 (xor_3_out, in_5, in_6);
  xor xor_4 (xor_4_out, in_7, in_8);
  xor xor_5 (out_10, xor_1_out, xor_2_out);
  xor xor_6 (xor_6_out, xor_3_out, xor_4_out);
  xor xor_7 (out_11, xor_6_out, in_9);
endmodule
