// Logisim project halfadder_fulladder.circ as structural Verilog: 1 circuit, main circuit main
module main (
  input  A,
  input  B,
  input  A_2,
  input  B_2,
  input  C,
  output SUM,
  output CARRY,
  output SUM_2,
  output CARRY_2
);

  wire and_2_out, and_3_out, xor_1_out;

  xor xor_1 (xor_1_out, A_2, B_2);
  xor xor_2 (SUM, A, B);
  buf and_1 (CARRY, A);  // AND_Gate
  and and_2 (and_2_out, xor_1_out, C);
  and and_3 (and_3_out, A_2, B_2);
  xor xor_3 (SUM_2, xor_1_out, C);
  or or_1 (CARRY_2, and_2_out, and_3_out);

  // Notes on the sheet:
  //   HALF ADDER
  //   FULL ADDER
endmodule
